# Fritzing sketch Bicyduino fritzing (saved by Fritzing 0.9.2b)
breadboards: 1

parts:
  Q1 = NPN-Transistor [package="TO92 [THT]"]
  Pro_Micro1 = Pro Micro

nets:
  N1: Q1.E, Pro_Micro1.VCC
  N2: Q1.B, Pro_Micro1.GND
  N3: Q1.C, Pro_Micro1.D18/A0

custom parts:
  Pro Micro: The SparkFun Pro Micro is a complete USB-based microcontoller development system, in a very small footprint, capable of implementing many types of projects. All programming can be done via the USB port.
